# Fritzing sketch Anti Snooze Nano (saved by Fritzing 0.9.3b)
breadboards: 1

parts:
  SEN1 = Pulse Sensor [package=SIP-3]
  SEN2 = Pulse Sensor [package=SIP-3]
  BAT5 = Battery Holders [package=battcon_12mm]
  J1 = Piezo Speaker
  U1 = SWITCH_SPDT [package=kps-1290]
  Part1 = Arduino Nano (Rev3.0) (ICSP)

nets:
  GND: SEN1.GND, SEN2.GND, BAT5.-, Part1.GND
  VCC: SEN1.VCC, SEN2.VCC, U1.S, Part1.5V
  N1: SEN1.Signal, Part1.D9
  N2: SEN2.Signal, Part1.D8
  N3: BAT5.+, U1.O
  N4: J1.pin1, Part1.A6
  N5: J1.pin2, Part1.A5

custom parts:
  Pulse Sensor: Pulse Sensor Optical Heart Beat Sensor
