# Fritzing sketch Anti-Snooze Uno (saved by Fritzing 0.9.3b)
circuit board: 8.46667cm x 5.64444cm
breadboards: 2

parts:
  Part1 = Arduino Uno (Rev3)
  J1 = Piezo Speaker
  SEN1 = Pulse Sensor [package=SIP-3]
  LED1 = LEDs [package=led10mm]
  S1 = Pushbutton [package="[THT]"]  # not connected
  R1 = Resistor [tolerance=±5% resistance=220 package="2010 [SMD]"]

nets:
  N1: Part1.A1, J1.pin2, R1.Pin_0
  N2: Part1.A2, SEN1.Signal
  5V: Part1.5V, SEN1.VCC
  N3: J1.pin1, SEN1.GND
  N4: LED1.C, R1.Pin_1

custom parts:
  Pulse Sensor: Pulse Sensor Optical Heart Beat Sensor

// code stored in the sketch: Heartbeat_code.ino
int a;

void setup() {
pinMode(A2,INPUT);
pinMode(A1,OUTPUT);
Serial.begin(4800);
}
void loop()
{
  a = analogRead(A2);
  Serial.println(a);
  delay(20);
  if(a<60)
  {
    digitalWrite(A1, HIGH);
  } 
  else 
  {
    digitalWrite(A1, LOW);
  }
  }
