# Fritzing sketch Pulse_sensor-fized (saved by Fritzing 0.9.3b)

parts:
  SEN1 = Pulse Sensor [package=SIP-3]
  J1 = female pin header, 2 pins [form="♀ (female)"]
  J2 = female pin header, 1 pin [form="♀ (female)"]

nets:
  N1: SEN1.GND, J1.pin1
  N2: SEN1.VCC, J1.pin2
  N3: SEN1.Signal, J2.pin1

custom parts:
  Pulse Sensor: Pulse Sensor Optical Heart Beat Sensor
